# Fritzing sketch flex-measure (saved by Fritzing 0.8.5b)
breadboards: 1

parts:
  R1 = Basic Flex Resistor
  Part1 = Arduino Uno (Rev3)
  R2 = Resistor [tolerance=±5% resistance=10k package=THT]

nets:
  N1: R1.Pin_2, Part1.5V
  N2: R1.pin_1, Part1.A0, R2.Pin_1
  N3: Part1.GND, R2.Pin_0
